# Fritzing sketch ArduinoMega (saved by Fritzing 0.9.3b)

parts:
  Parça3 = Arduino Mega 2560 (Rev3)
  SP1 = SPEAKER [package=pcb_mount_speaker]
  DFPlayer_Mini1 = DFPlayer MINI [package="DIP (Dual Inline) [THT]"]
  LCD2 = LCD screen
  LCM1602_IIC1 = LCM1602 IIC [part_number="LCM1602 IIC" chip_label="LCM1602 IIC" package="DIP (Dual Inline) [THT]"]
  SD_card_module1 = SD Card Module
  Driver1 = 28BYJ-48 Driver Module [part_number=ULN2003 package=THT]
  SM1 = 28BYJ-48 Stepper Motor [part_number=28BYJ-48]  # not connected

nets:
  N1: Parça3.D21/SCL, LCM1602_IIC1.SCL
  N2: Parça3.D20/SDA, LCM1602_IIC1.SDA
  N3: Parça3.D10_PWM, SD_card_module1.CS
  5V: Parça3.5V, LCM1602_IIC1.VCC
  GND: Parça3.GND, LCM1602_IIC1.GND
  N4: Parça3.D4_PWM, Driver1.IN1
  N5: Parça3.D5_PWM, Driver1.IN2
  N6: Parça3.D6_PWM, Driver1.IN3
  N7: Parça3.D7_PWM, Driver1.IN4
  N8: SP1.+, DFPlayer_Mini1.SPK2
  N9: SP1.-, DFPlayer_Mini1.SPK1
  VSS: LCD2.VSS, LCM1602_IIC1.VSS
  VDD: LCD2.VDD, LCM1602_IIC1.VDD
  N10: LCD2.V0, LCM1602_IIC1.V0
  N11: LCD2.RS, LCM1602_IIC1.RS
  N12: LCD2.R/W, LCM1602_IIC1.RW
  N13: LCD2.E, LCM1602_IIC1.E
  N14: LCD2.DB0, LCM1602_IIC1.D0
  N15: LCD2.DB1, LCM1602_IIC1.D1
  N16: LCD2.DB2, LCM1602_IIC1.D2
  N17: LCD2.DB3, LCM1602_IIC1.D3
  N18: LCD2.DB4, LCM1602_IIC1.D4
  N19: LCD2.DB5, LCM1602_IIC1.D5
  N20: LCD2.DB6, LCM1602_IIC1.D6
  N21: LCD2.DB7, LCM1602_IIC1.D7
  N22: LCD2.LED+, LCM1602_IIC1.A
  N23: LCD2.LED-, LCM1602_IIC1.K
  N24: LCM1602_IIC1.LED_A, LCM1602_IIC1.LED_B

custom parts:
  DFPlayer MINI: MP3 module by DFRobot.com for playing Music from an SD-Card. Supports WAV and MP3 files.
  LCM1602 IIC: I2C-Module to use a 1602 or 2004 LCD on with the wire.h libory Serial LCD Modul
  SD Card Module: SD Card Module Slot Socket Reader For Arduino ARM MCU
  28BYJ-48 Driver Module: Generic male header
  28BYJ-48 Stepper Motor: Unipolar Stepper Motor 28BYJ-48 Top coil - pink & orange Bottom coil - blue & yellow Common rail - red Connector pins: blue - pink - yellow - orange - red
